// Logisim project lock_logic.circ as structural Verilog: 7 circuits, main circuit button_filter
module main (
  input  x1,
  input  x0,
  input  clk,
  input  reset,
  output Output_1
);

  wire Next_State_1_d0, Next_State_1_d1, q0_q, q1_q;

  Next_State Next_State_1 (.x1(x1), .x0(x0), .q0(q0_q), .q1(q1_q), .d1(Next_State_1_d1), .d0(Next_State_1_d0));
  Register #(.width(1)) q1 (.D(Next_State_1_d1), .clk(clk), .Q(q1_q), .clr(reset));  // open: en
  Register #(.width(1)) q0 (.D(Next_State_1_d0), .clk(clk), .Q(q0_q), .clr(reset));  // open: en
  Output_logic ABAC (.x0(x0), .x1(x1), .q1(q1_q), .q0(q0_q), .Output(Output_1));
endmodule

module Next_State (
  input  x1,
  input  x0,
  input  q0,
  input  q1,
  output d1,
  output d0
);

  wire and_1_out, and_2_out, not_1_out, not_2_out, not_3_out;

  not not_1 (not_1_out, x1);
  not not_2 (not_2_out, x0);
  not not_3 (not_3_out, q0);
  and and_1 (and_1_out, q1, not_3_out, not_2_out, not_1_out);
  and and_2 (and_2_out, q0, x0);
  and and_3 (d0, not_1_out, not_2_out);
  or or_1 (d1, and_1_out, and_2_out);
endmodule

module Output_logic (
  input  x0,
  input  x1,
  input  q1,
  input  q0,
  output Output
);

  and and_1 (Output, q0, q1, x1);
endmodule

module debounce_board (
  input  reset,
  input  tl_in,
  input  clk,
  output tl_out
);

  wire comparator_1_eq, comparator_2_eq;
  wire [18:0] counter_1_q;

  Counter #(.max('h7ffff), .ongoal("stay"), .width(19)) counter_1 (
    .clr(reset), .load(1'b0), .up(tl_in), .count(1'b1), .clk(clk), .D({19{1'b0}}), .Q(counter_1_q));  // open: carry
  // Probe on counter_1_q
  Comparator #(.mode("unsigned"), .width(19)) comparator_1 (
    .a(counter_1_q), .b({19{1'b1}}), .eq(comparator_1_eq));  // open: gt, lt
  Comparator #(.mode("unsigned"), .width(19)) comparator_2 (
    .a(counter_1_q), .b({19{1'b0}}), .eq(comparator_2_eq));  // open: gt, lt
  S_R_Flip_Flop s_r_ff_1 (.S(comparator_1_eq), .R(comparator_2_eq), .clk(clk), .Q(tl_out));  // open: reset, Qn, preset

  // Notes on the sheet:
  //   Internal counter value
endmodule

module debounce_sim (
  input  reset,
  input  tl_in,
  input  clk,
  output tl_out
);

  wire comparator_1_eq, comparator_2_eq;
  wire [2:0] counter_1_q;

  Counter #(.max('h7), .ongoal("stay"), .width(3)) counter_1 (
    .clr(reset), .load(1'b0), .up(tl_in), .count(1'b1), .clk(clk), .D(3'b000), .Q(counter_1_q));  // open: carry
  // Probe on counter_1_q
  Comparator #(.mode("unsigned"), .width(3)) comparator_1 (
    .a(counter_1_q), .b(3'b111), .eq(comparator_1_eq));  // open: gt, lt
  Comparator #(.mode("unsigned"), .width(3)) comparator_2 (
    .a(counter_1_q), .b(3'b000), .eq(comparator_2_eq));  // open: gt, lt
  S_R_Flip_Flop s_r_ff_1 (.S(comparator_1_eq), .R(comparator_2_eq), .clk(clk), .Q(tl_out));  // open: reset, Qn, preset

  // Notes on the sheet:
  //   Internal counter value
endmodule

module top2 (
  input  x1,
  input  x0,
  input  reset,
  output out_4
);

  wire button_filter_1_tl_out, button_filter_2_tl_out, clk_out;

  Clock clk (.out(clk_out));
  button_filter button_filter_1 (.reset(reset), .tl_in(x1), .clk(clk_out), .tl_out(button_filter_1_tl_out));
  button_filter button_filter_2 (.reset(reset), .tl_in(x0), .clk(clk_out), .tl_out(button_filter_2_tl_out));
  main main_1 (
    .x1(button_filter_1_tl_out), .x0(button_filter_2_tl_out), .clk(clk_out), .reset(reset), .Output_1(out_4));
endmodule

module button_filter (
  input  reset,
  input  tl_in,
  input  clk,
  output tl_out
);

  wire d_ff_1_q, debounce_board_1_tl_out, not_1_out;

  debounce_board debounce_board_1 (.reset(reset), .tl_in(tl_in), .clk(clk), .tl_out(debounce_board_1_tl_out));
  D_Flip_Flop d_ff_1 (.D(debounce_board_1_tl_out), .clk(clk), .Q(d_ff_1_q), .reset(reset));  // open: Qn, preset
  not not_1 (not_1_out, d_ff_1_q);
  buf and_1 (tl_out, debounce_board_1_tl_out);  // AND_Gate
endmodule
