// Logisim project bit_counter_display.circ as structural Verilog: 4 circuits, main circuit main
module main (
  input  Input_1,
  input  Input_2,
  input  Input_3,
  input  Input_4,
  input  Input_5,
  input  Input_6,
  input  Input_7,
  input  Input_8,
  input  Input_9,
  output Output_1,
  output Output_2,
  output Output_3,
  output Output_4,
  output COUToutput,
  output Output_5,
  output Output_6,
  output const1,
  output Output_7,
  output const2,
  output const3,
  output const4
);

  wire FourBitCounter_1_s0, FourBitCounter_1_s1, FourBitCounter_1_s2, FourBitCounter_1_s3;

  FourBitCounter FourBitCounter_1 (
    .A0(Input_1), .B0(Input_2), .Cin(Input_3), .A1(Input_4), .B1(Input_5), .A2(Input_6), .B2(Input_7),
    .A3(Input_8), .B3(Input_9), .S0(FourBitCounter_1_s0), .S1(FourBitCounter_1_s1), .S2(FourBitCounter_1_s2),
    .S3(FourBitCounter_1_s3), .COUT(COUToutput));
  sseg sseg_1 (
    .a(FourBitCounter_1_s0), .b(FourBitCounter_1_s1), .c(FourBitCounter_1_s2), .d(FourBitCounter_1_s3),
    .sa(Output_1), .sb(Output_2), .sc(Output_3), .sd(Output_4), .se(Output_5), .sf(Output_6), .sg(Output_7));

  assign const1 = 1'b1;
  assign const2 = 1'b0;
  assign const3 = 1'b0;
  assign const4 = 1'b0;
endmodule

module Onebit (
  input  Input_1,
  input  Input_2,
  input  Input_3,
  output Output_1,
  output Output_2
);

  wire and_1_out, and_2_out, xor_1_out;

  xor xor_1 (xor_1_out, Input_1, Input_2);
  and and_1 (and_1_out, Input_1, Input_2);
  xor xor_2 (Output_1, xor_1_out, Input_3);
  and and_2 (and_2_out, xor_1_out, Input_3);
  or or_1 (Output_2, and_2_out, and_1_out);
endmodule

module sseg (
  input  a,
  input  b,
  input  c,
  input  d,
  output sa,
  output sb,
  output sc,
  output sd,
  output se,
  output sf,
  output sg
);

  wire and_1_out, and_2_out, and_3_out, and_4_out, and_5_out, and_6_out, and_7_out, and_8_out, and_9_out,
       and_10_out, and_11_out, and_12_out, and_13_out, and_14_out, and_15_out, and_16_out, not_1_out,
       not_2_out, not_3_out, not_4_out;

  not not_1 (not_1_out, a);
  not not_2 (not_2_out, b);
  not not_3 (not_3_out, c);
  not not_4 (not_4_out, d);
  and and_1 (and_1_out, not_1_out, not_2_out, not_3_out);
  and and_2 (and_2_out, a, c);
  and and_3 (and_3_out, a, b);
  and and_4 (and_4_out, not_1_out, not_2_out);
  or or_1 (sc, a, c, not_2_out);
  and and_5 (and_5_out, b, not_1_out);
  and and_6 (and_6_out, b, not_3_out, not_4_out);
  and and_7 (and_7_out, not_1_out, not_3_out, not_4_out);
  and and_8 (and_8_out, c, a, not_2_out);
  and and_9 (and_9_out, not_3_out, not_1_out, not_2_out);
  and and_10 (and_10_out, b, not_1_out);
  and and_11 (and_11_out, c, not_2_out);
  and and_12 (and_12_out, not_2_out, not_1_out);
  and and_13 (and_13_out, not_1_out, c);
  and and_14 (and_14_out, c, not_2_out);
  and and_15 (and_15_out, not_3_out, b);
  and and_16 (and_16_out, b, not_1_out);
  or or_2 (sa, d, b, and_1_out, and_2_out);
  or or_3 (sb, not_3_out, and_3_out, and_4_out);
  or or_4 (sd, d, and_5_out, and_6_out, and_7_out, and_8_out);
  or or_5 (se, and_9_out, and_10_out);
  or or_6 (sf, d, and_11_out, and_12_out, and_13_out);
  or or_7 (sg, d, and_14_out, and_15_out, and_16_out);
endmodule

module FourBitCounter (
  input  A0,
  input  B0,
  input  Cin,
  input  A1,
  input  B1,
  input  A2,
  input  B2,
  input  A3,
  input  B3,
  output S0,
  output S1,
  output S2,
  output S3,
  output COUT
);

  wire main_1_output_2, main_2_output_2, main_3_output_2;

  Onebit main_1 (.Input_1(A0), .Input_2(B0), .Input_3(Cin), .Output_1(S0), .Output_2(main_1_output_2));
  Onebit main_2 (.Input_1(A1), .Input_2(B1), .Input_3(main_1_output_2), .Output_1(S1), .Output_2(main_2_output_2));
  Onebit main_3 (.Input_1(A2), .Input_2(B2), .Input_3(main_2_output_2), .Output_1(S2), .Output_2(main_3_output_2));
  Onebit main_4 (.Input_1(A3), .Input_2(B3), .Input_3(main_3_output_2), .Output_1(S3), .Output_2(COUT));
endmodule
