// Logisim project bit_sequence_search.circ.circ as structural Verilog: 6 circuits, main circuit main
module main (
  input  sw,
  input  clk,
  input  reset,
  output led
);

  wire next_state_1_d0, next_state_1_d1, next_state_1_d2, q0_q, q1_q, q2_q;

  next_state next_state_1 (
    .sw(sw), .q2(q2_q), .q1(q1_q), .q0(q0_q), .d2(next_state_1_d2), .d1(next_state_1_d1), .d0(next_state_1_d0));
  Register #(.width(1)) q2 (.D(next_state_1_d2), .clk(clk), .Q(q2_q), .clr(reset));  // open: en
  Register #(.width(1)) q1 (.D(next_state_1_d1), .clk(clk), .Q(q1_q), .clr(reset));  // open: en
  Register #(.width(1)) q0 (.D(next_state_1_d0), .clk(clk), .Q(q0_q), .clr(reset));  // open: en
  output_logic output_logic_1 (.q2(q2_q), .q1(q1_q), .q0(q0_q), .y(led));
endmodule

module next_state (
  input  sw,
  input  q2,
  input  q1,
  input  q0,
  output d2,
  output d1,
  output d0
);

  wire and_1_out, and_2_out, and_3_out, and_4_out, and_5_out, and_6_out, and_7_out, and_8_out, and_9_out,
       and_10_out, not_1_out, not_2_out, not_3_out, not_4_out;

  not not_1 (not_1_out, sw);
  not not_2 (not_2_out, q2);
  not not_3 (not_3_out, q1);
  not not_4 (not_4_out, q0);
  and and_1 (and_1_out, not_1_out, q0);
  and and_2 (and_2_out, not_1_out, not_2_out, q1);
  and and_3 (and_3_out, sw, q2, not_3_out, not_4_out);
  and and_4 (and_4_out, q2, q1, q0);
  and and_5 (and_5_out, sw, not_2_out, q1);
  and and_6 (and_6_out, q2, not_3_out, q0);
  and and_7 (and_7_out, sw, not_3_out, q0);
  and and_8 (and_8_out, not_1_out, q1, q0);
  and and_9 (and_9_out, sw, not_4_out);
  and and_10 (and_10_out, q1, sw);
  or or_1 (d2, and_1_out, and_2_out, and_3_out, and_4_out);
  or or_2 (d1, and_5_out, and_6_out, and_7_out, and_8_out);
  or or_3 (d0, and_9_out, and_10_out);
endmodule

module output_logic (
  input  q2,
  input  q1,
  input  q0,
  output y
);

  and and_1 (y, q1, q2);
endmodule

module debounce_board (
  input  reset,
  input  tl_in,
  input  clk,
  output tl_out
);

  wire comparator_1_eq, comparator_2_eq;
  wire [18:0] counter_1_q;

  Counter #(.max('h7ffff), .ongoal("stay"), .width(19)) counter_1 (
    .clr(reset), .load(1'b0), .up(tl_in), .count(1'b1), .clk(clk), .D({19{1'b0}}), .Q(counter_1_q));  // open: carry
  // Probe on counter_1_q
  Comparator #(.mode("unsigned"), .width(19)) comparator_1 (
    .a(counter_1_q), .b({19{1'b1}}), .eq(comparator_1_eq));  // open: gt, lt
  Comparator #(.mode("unsigned"), .width(19)) comparator_2 (
    .a(counter_1_q), .b({19{1'b0}}), .eq(comparator_2_eq));  // open: gt, lt
  S_R_Flip_Flop s_r_ff_1 (.S(comparator_1_eq), .R(comparator_2_eq), .clk(clk), .Q(tl_out));  // open: reset, Qn, preset

  // Notes on the sheet:
  //   Internal counter value
endmodule

module debounce_sim (
  input  reset,
  input  tl_in,
  input  clk,
  output tl_out
);

  wire comparator_1_eq, comparator_2_eq;
  wire [2:0] counter_1_q;

  Counter #(.max('h7), .ongoal("stay"), .width(3)) counter_1 (
    .clr(reset), .load(1'b0), .up(tl_in), .count(1'b1), .clk(clk), .D(3'b000), .Q(counter_1_q));  // open: carry
  // Probe on counter_1_q
  Comparator #(.mode("unsigned"), .width(3)) comparator_1 (
    .a(counter_1_q), .b(3'b111), .eq(comparator_1_eq));  // open: gt, lt
  Comparator #(.mode("unsigned"), .width(3)) comparator_2 (
    .a(counter_1_q), .b(3'b000), .eq(comparator_2_eq));  // open: gt, lt
  S_R_Flip_Flop s_r_ff_1 (.S(comparator_1_eq), .R(comparator_2_eq), .clk(clk), .Q(tl_out));  // open: reset, Qn, preset

  // Notes on the sheet:
  //   Internal counter value
endmodule

module top (
  input  sw,
  input  clk_button,
  input  reset,
  output led
);

  wire clk_out, debounce_board_1_tl_out;

  Clock clk (.out(clk_out));
  debounce_board debounce_board_1 (.reset(reset), .tl_in(clk_button), .clk(clk_out), .tl_out(debounce_board_1_tl_out));
  main main_1 (.sw(sw), .clk(debounce_board_1_tl_out), .reset(reset), .led(led));
endmodule
